# Fritzing sketch maxclock (saved by Fritzing 1.0.4)
circuit board: 8.46667cm x 5.64444cm
breadboards: 1

parts:
  M1 = DOIT Esp32 DevKit v1 (30 pins long, 11 pins width) [part_number=ESP32S-PIN30]
  J1 = female pin header, 5 pins [form="♀ (female)"]
  IC1 = Voltage Regulator [package=to220-igo]
  J2 = Power Jack [package=power_jack_pth_lock]
  R1 = Photocell (LDR) [power=0.25W dark_resistance_@0.01lx=300kΩ light_resistance_@100lx=400Ω luminance=10lx package=THT]
  R2 = Resistor [tolerance=±5% power=0.25W resistance=10k package=THT]
  C2 = Electrolytic Capacitor [capacitance=0.47mF voltage=35V package="100 mil [THT, electrolytic]"]
  C3 = Electrolytic Capacitor [capacitance=0.47µF voltage=35V package="100 mil [THT, electrolytic]"]
  X1 = USB Connectors [package=usb-a-h]
  R3 = Resistor [tolerance=±5% power=0.25W resistance=100k package=THT]
  R4 = Resistor [tolerance=±5% power=0.25W resistance=100k package=THT]

nets:
  N1: M1.3V3, J1.pin1, R1.pin_1
  GND: M1.GND, J1.pin2, IC1.GND, J2.GND, R2.Pin_0, C2.-, C3.-, X1.GND
  N2: M1.D15, J1.pin4
  N3: M1.VP, R1.pin_0, R2.Pin_1
  N4: M1.D14, J1.pin5
  N5: M1.D13, J1.pin3
  N6: M1.VIN, IC1.OUT, C3.+, X1.VBUS, R3.Pin_1, R4.Pin_0
  N7: IC1.IN, J2.PWR, C2.+
  N8: X1.D-, R3.Pin_0
  N9: X1.D+, R4.Pin_1

custom parts:
  DOIT Esp32 DevKit v1 (30 pins long, 11 pins width): The DOIT Esp32 DevKit v1 is one of the development board created by DOIT to evaluate the ESP-WROOM-32 module. It is based on the ESP32 microcontroller that boasts Wifi, Bluetooth, Ethernet and Low Power support all in a single chip. (vanepp) made breadboard work, adjusted pin numbering and labels and reduced size of schematic and cleaned up pcb. This chip is 30pins long (2 x15) and 11 pins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
